# Fritzing sketch esquematico_electro (saved by Fritzing 0.9.3b)
breadboards: 1

parts:
  Componente1 = BluePill
  LCD1 = TFT 1.8 inch 160x128 w SD
  J1 = Piezo Speaker
  R1 = Temperature Sensor (Thermistor) [thermistor_type=NTC package=THT]
  R2 = Resistor [tolerance=±5% resistance=220 package=THT]
  Q1 = Basic FET P-Channel [package="D2Pak [SMD]"]
  S1 = SWITCH-MOMENTARY-2 [package=tactile-pth-12mm]
  Q2 = Basic FET P-Channel [package="D2Pak [SMD]"]

nets:
  N1: Componente1.A0, R1.pin_0, R2.Pin_0
  N2: Componente1.A3, LCD1.pin_5
  N3: Componente1.A4, LCD1.pin3
  N4: Componente1.A5, LCD1.pin_7
  N5: Componente1.A7, LCD1.pin_6
  N6: Componente1.3V3, LCD1.pin_1, LCD1.pin_8, R1.pin_1
  N7: Componente1.GND2, LCD1.pin2, J1.pin1, R2.Pin_1, S1.1
  N8: Componente1.A10, S1.2
  N9: Componente1.A9, Q2.Gate
  N10: Componente1.A8, Q1.Gate
  N11: Componente1.B15, J1.pin2
  N12: Componente1.A2, LCD1.pin4

custom parts:
  TFT 1.8 inch 160x128 w SD: This is a generic 1.8 tft spi lcd display available on ebay and others. The 1.8" display has 128x160 color pixels.
