# Fritzing sketch esquematico_moskvich (saved by Fritzing 0.9.3b)
breadboards: 1

parts:
  Componente1 = BluePill
  J1 = Piezo Speaker
  R1 = Temperature Sensor (Thermistor) [thermistor_type=NTC package=THT]
  R2 = Resistor [tolerance=±5% resistance=6.75k package=THT]
  Config = SWITCH-MOMENTARY-2 [package=tactile-pth-12mm]
  R3 = Resistor [tolerance=±5% resistance=4.7k package=THT]
  D1 = Diode [package=diode-hv]
  R4 = Resistor [tolerance=±5% resistance=560 package=THT]
  R5 = Resistor [tolerance=±5% resistance=240 package=THT]
  JP1 = RCA [package=rca]
  Q1 = NPN-Transistor [package="TO92 [THT]"]
  D2 = Diode [package=diode-hv]
  R6 = Resistor [tolerance=±5% resistance=220 package=THT]
  BAT1 = BC9VPC [package=bc9vpc]
  R7 = Resistor [tolerance=±5% resistance=1k package=THT]
  R8 = Resistor [tolerance=±5% resistance=4.7k package=THT]
  R9 = Resistor [tolerance=±5% resistance=4.7k package=THT]
  R10 = Resistor [tolerance=±5% resistance=1k package=THT]
  Reversa = SWITCH-MOMENTARY-2 [package=tactile_switch_tall]
  C1 = Electrolytic Capacitor [capacitance=4.7µF package="100 mil [THT, electrolytic]"]
  C2 = Electrolytic Capacitor [capacitance=4.7µF package="100 mil [THT, electrolytic]"]
  C3 = Electrolytic Capacitor [capacitance=4.7µF package="100 mil [THT, electrolytic]"]

nets:
  N1: Componente1.A0, R3.Pin_0, D1.A, C1.+
  N2: Componente1.A1, R4.Pin_0
  N3: Componente1.A7, R5.Pin_1
  N4: Componente1.3V31, R2.Pin_1, D1.C
  N5: Componente1.B6, D2.A
  N6: Componente1.B5, R9.Pin_1, R10.Pin_0, C3.+
  N7: Componente1.A10, Config.2
  N8: Componente1.A2, R7.Pin_1, R8.Pin_1, C2.+
  N9: J1.pin1, Q1.C
  N10: J1.pin2, BAT1.V+, R8.Pin_0, Reversa.2
  N11: R1.pin_0, Config.1, JP1.SHELL, Q1.E, BAT1.V-, R7.Pin_0, R10.Pin_1, C1.-, C2.-, C3.-
  N12: R1.pin_1, R2.Pin_0, R3.Pin_1
  N13: R4.Pin_1, R5.Pin_0, JP1.PIN
  N14: Q1.B, R6.Pin_1
  N15: D2.C, R6.Pin_0
  N16: R9.Pin_0, Reversa.1

notes:
  Sensor de la reversa
